// Logisim project dz_1.circ as structural Verilog: 1 circuit, main circuit main
module main (
  input  in_1,
  input  in_2,
  input  in_3,
  input  in_4,
  input  in_5,
  input  in_6,
  input  in_7,
  input  in_8,
  input  in_9,
  input  in_10,
  output out_11,
  output out_12
);

  wire and_2_out, and_3_out, and_4_out, and_5_out, and_6_out, and_7_out, and_8_out, and_9_out, and_10_out,
       and_11_out, and_12_out, and_13_out, and_14_out, and_15_out, and_16_out, and_17_out, and_18_out,
       and_19_out, and_20_out, and_21_out, and_22_out, and_23_out, not_1_out, not_2_out, not_3_out,
       not_4_out, not_5_out, not_6_out, not_7_out, not_8_out, not_9_out, not_10_out, not_11_out, not_12_out,
       not_13_out, not_14_out, not_15_out, not_16_out, not_17_out, not_18_out, not_19_out, not_20_out,
       not_21_out, not_22_out, not_23_out, not_24_out, not_25_out, not_26_out, not_27_out, not_28_out,
       not_29_out, not_30_out, not_31_out, not_32_out, not_33_out, not_34_out, not_35_out, not_36_out,
       not_37_out, not_38_out, not_39_out, not_40_out, not_41_out, not_42_out, not_43_out, not_44_out,
       not_45_out, not_46_out, not_47_out, not_48_out, not_49_out, not_50_out, not_51_out, not_52_out,
       not_53_out, not_54_out, not_55_out, not_56_out, not_57_out, not_58_out, not_59_out, not_60_out,
       not_61_out, not_62_out, not_63_out, not_64_out, not_65_out, not_66_out, not_67_out, not_68_out,
       not_69_out, not_70_out, not_71_out, not_72_out, not_73_out, or_1_out, or_2_out, or_3_out, or_4_out,
       or_5_out, or_6_out, or_7_out, or_8_out, or_9_out, or_10_out;

  or or_1 (or_1_out, in_5, in_4, in_3, in_2, in_1);
  not not_1 (not_1_out, in_4);
  or or_2 (or_2_out, in_5, not_1_out, in_3, in_2, in_1);
  or or_3 (or_3_out, in_5, in_4, not_2_out, in_2, in_1);
  not not_2 (not_2_out, in_3);
  not not_3 (not_3_out, in_4);
  not not_4 (not_4_out, in_3);
  or or_4 (or_4_out, in_5, not_3_out, not_4_out, in_2, in_1);
  or or_5 (or_5_out, in_5, in_4, in_3, not_5_out, in_1);
  not not_5 (not_5_out, in_2);
  not not_6 (not_6_out, in_5);
  not not_7 (not_7_out, in_3);
  or or_6 (or_6_out, not_6_out, in_4, not_7_out, not_8_out, in_1);
  not not_8 (not_8_out, in_2);
  not not_9 (not_9_out, in_4);
  or or_7 (or_7_out, in_5, not_9_out, not_10_out, not_11_out, in_1);
  not not_10 (not_10_out, in_3);
  not not_11 (not_11_out, in_2);
  not not_12 (not_12_out, in_5);
  not not_13 (not_13_out, in_4);
  not not_14 (not_14_out, in_3);
  or or_8 (or_8_out, not_12_out, not_13_out, not_14_out, not_15_out, in_1);
  not not_15 (not_15_out, in_2);
  not not_16 (not_16_out, in_5);
  not not_17 (not_17_out, in_4);
  or or_9 (or_9_out, not_16_out, not_17_out, in_3, in_2, not_18_out);
  not not_18 (not_18_out, in_1);
  not not_19 (not_19_out, in_5);
  not not_20 (not_20_out, in_4);
  not not_21 (not_21_out, in_3);
  or or_10 (or_10_out, not_19_out, not_20_out, not_21_out, in_2, not_22_out);
  not not_22 (not_22_out, in_1);
  and and_1 (out_11, or_1_out, or_2_out, or_3_out, or_4_out, or_5_out, or_6_out, or_7_out, or_8_out, or_9_out, or_10_out);
  not not_23 (not_23_out, in_9);
  not not_24 (not_24_out, in_8);
  not not_25 (not_25_out, in_7);
  not not_26 (not_26_out, in_6);
  not not_27 (not_27_out, in_8);
  not not_28 (not_28_out, in_7);
  not not_29 (not_29_out, in_6);
  not not_30 (not_30_out, in_9);
  not not_31 (not_31_out, in_8);
  not not_32 (not_32_out, in_6);
  not not_33 (not_33_out, in_6);
  not not_34 (not_34_out, in_9);
  not not_35 (not_35_out, in_8);
  not not_36 (not_36_out, in_6);
  not not_37 (not_37_out, in_10);
  not not_38 (not_38_out, in_8);
  not not_39 (not_39_out, in_6);
  not not_40 (not_40_out, in_8);
  not not_41 (not_41_out, in_6);
  not not_42 (not_42_out, in_10);
  not not_43 (not_43_out, in_9);
  not not_44 (not_44_out, in_6);
  not not_45 (not_45_out, in_10);
  not not_46 (not_46_out, in_9);
  not not_47 (not_47_out, in_8);
  not not_48 (not_48_out, in_7);
  not not_49 (not_49_out, in_9);
  not not_50 (not_50_out, in_8);
  not not_51 (not_51_out, in_7);
  not not_52 (not_52_out, in_10);
  not not_53 (not_53_out, in_8);
  not not_54 (not_54_out, in_7);
  not not_55 (not_55_out, in_10);
  not not_56 (not_56_out, in_9);
  not not_57 (not_57_out, in_7);
  not not_58 (not_58_out, in_9);
  not not_59 (not_59_out, in_7);
  not not_60 (not_60_out, in_10);
  not not_61 (not_61_out, in_7);
  not not_62 (not_62_out, in_10);
  not not_63 (not_63_out, in_9);
  not not_64 (not_64_out, in_8);
  not not_65 (not_65_out, in_9);
  not not_66 (not_66_out, in_8);
  not not_67 (not_67_out, in_10);
  not not_68 (not_68_out, in_8);
  not not_69 (not_69_out, in_8);
  not not_70 (not_70_out, in_10);
  not not_71 (not_71_out, in_9);
  not not_72 (not_72_out, in_9);
  not not_73 (not_73_out, in_10);
  and and_2 (and_2_out, in_10, not_23_out, not_24_out, not_25_out, not_26_out);
  and and_3 (and_3_out, in_10, in_9, not_27_out, not_28_out, not_29_out);
  and and_4 (and_4_out, in_10, not_30_out, not_31_out, in_7, not_32_out);
  and and_5 (and_5_out, in_10, in_9, in_8, in_7, not_33_out);
  and and_6 (and_6_out, in_10, not_34_out, not_35_out, in_7, not_36_out);
  and and_7 (and_7_out, not_37_out, in_9, not_38_out, in_7, not_39_out);
  and and_8 (and_8_out, in_10, in_9, not_40_out, in_7, not_41_out);
  and and_9 (and_9_out, not_42_out, not_43_out, in_8, in_7, not_44_out);
  and and_10 (and_10_out, not_45_out, not_46_out, not_47_out, not_48_out, in_6);
  and and_11 (and_11_out, in_10, not_49_out, not_50_out, not_51_out, in_6);
  and and_12 (and_12_out, not_52_out, in_9, not_53_out, not_54_out, in_6);
  and and_13 (and_13_out, not_55_out, not_56_out, in_8, not_57_out, in_6);
  and and_14 (and_14_out, in_10, not_58_out, in_8, not_59_out, in_6);
  and and_15 (and_15_out, not_60_out, in_9, in_8, not_61_out, in_6);
  and and_16 (and_16_out, not_62_out, not_63_out, not_64_out, in_7, in_6);
  and and_17 (and_17_out, in_10, not_65_out, not_66_out, in_7, in_6);
  and and_18 (and_18_out, not_67_out, in_9, not_68_out, in_7, in_6);
  and and_19 (and_19_out, in_10, in_9, not_69_out, in_7, in_6);
  and and_20 (and_20_out, not_70_out, not_71_out, in_8, in_7, in_6);
  and and_21 (and_21_out, in_10, not_72_out, in_8, in_7, in_6);
  and and_22 (and_22_out, not_73_out, in_9, in_8, in_7, in_6);
  and and_23 (and_23_out, in_10, in_9, in_8, in_7, in_6);
  or or_11 (out_12, and_2_out, and_3_out, and_4_out, and_5_out, and_6_out, and_7_out, and_8_out, and_9_out, and_10_out, and_11_out, and_12_out, and_14_out, and_15_out, and_16_out, and_17_out, and_18_out, and_19_out, and_20_out, and_21_out, and_22_out, and_23_out, and_13_out);
endmodule
